# Fritzing sketch ShiftRegister (saved by Fritzing 0.9.3b)
breadboards: 1

parts:
  IC1 = SHIFT REGISTER [package=dil16]
  Q1 = NPN-Transistor [package="TO92 [THT]"]
  Q2 = NPN-Transistor [package="TO92 [THT]"]
  Q3 = NPN-Transistor [package="TO92 [THT]"]
  Q4 = NPN-Transistor [package="TO92 [THT]"]
  Q5 = NPN-Transistor [package="TO92 [THT]"]
  Q6 = NPN-Transistor [package="TO92 [THT]"]
  Q7 = NPN-Transistor [package="TO92 [THT]"]
  Q8 = NPN-Transistor [package="TO92 [THT]"]
  R1 = Resistor [tolerance=±5% resistance=220 package="2010 [SMD]"]
  R2 = Resistor [tolerance=±5% resistance=220 package="2010 [SMD]"]
  R3 = Resistor [tolerance=±5% resistance=220 package="2010 [SMD]"]
  R4 = Resistor [tolerance=±5% resistance=220 package="2010 [SMD]"]
  R5 = Resistor [tolerance=±5% resistance=220 package="2010 [SMD]"]
  R6 = Resistor [tolerance=±5% resistance=220 package="2010 [SMD]"]
  R7 = Resistor [tolerance=±5% resistance=220 package="2010 [SMD]"]
  R8 = Resistor [tolerance=±5% resistance=220 package="2010 [SMD]"]

nets:
  N1: IC1.VCC, Q1.C, Q2.C, Q3.C, Q4.C, Q5.C, Q6.C, Q7.C, Q8.C
  N2: Q1.E, R2.Pin_0
  N3: Q2.E, R4.Pin_0
  N4: Q3.E, R6.Pin_0
  N5: Q4.E, R1.Pin_0
  N6: Q5.E, R3.Pin_0
  N7: Q6.E, R8.Pin_0
  N8: Q7.E, R5.Pin_0
  N9: Q8.E, R7.Pin_0
